# Fritzing sketch Moisture_sensor (saved by Fritzing 1.0.4)
breadboards: 1

parts:
  Grove1 = Grove OLED 128x96
  LED1 = RGB LED (com. cathode, rbg) [color="Red (633nm)" current=0.030A package="5 mm [THT]"]
  Bauteil1 = Arduino Uno (Rev3) - ICSP
  R1 = Resistor [tolerance=±5% resistance=220 package="2010 [SMD]"]
  R2 = Resistor [tolerance=±5% resistance=220 package="2010 [SMD]"]
  R3 = Resistor [tolerance=±5% resistance=220 package="2010 [SMD]"]
  Chirp!_Soil_Moisture_Sensor1 = Chirp! Soil Moisture Sensor v2.7.3

nets:
  GND: Grove1.GND, LED1.common_cathode, Bauteil1.GND, Chirp!_Soil_Moisture_Sensor1.pin_5
  VCC: Grove1.VCC, Bauteil1.3V3
  N1: Grove1.SDA, Bauteil1.A5/SCL
  N2: Grove1.SCL, Bauteil1.A4/SDA
  N3: LED1.red_anode, R1.Pin_1
  N4: LED1.blue_anode, R2.Pin_1
  N5: LED1.green_anode, R3.Pin_1
  N6: Bauteil1.A0, Chirp!_Soil_Moisture_Sensor1.pin_3
  N7: Bauteil1.D0/RX, R1.Pin_0
  N8: Bauteil1.D1/TX, R2.Pin_0
  N9: Bauteil1.D2, R3.Pin_0
  N10: Bauteil1.5V, Chirp!_Soil_Moisture_Sensor1.Pin_1
